// Logisim project 3A.circ as structural Verilog: 1 circuit, main circuit main
module main (
  input  in_1,
  input  in_2,
  input  in_3,
  input  [1:0] A_B,
  output out_5
);

  wire and_1_out, undriven;

  and and_1 (and_1_out, in_1, in_2);
  Multiplexer #(.select(2)) multiplexer_1 (
    .in0(1'b0), .in1(1'b0), .in2(and_1_out), .in3(1'b1), .out(out_5), .sel(A_B), .en(undriven));
endmodule
