// Logisim project 3C.circ as structural Verilog: 1 circuit, main circuit main
module main (
  input  C,
  input  D,
  input  in_3,
  input  [1:0] A_B,
  output out_5
);

  wire and_1_out;

  and and_1 (and_1_out, C, D);
  Multiplexer #(.select(2)) multiplexer_1 (
    .in0(and_1_out), .in1(and_1_out), .in2(1'b0), .in3(1'b1), .out(out_5), .sel(A_B), .en(in_3));
endmodule
