// Logisim project Adder-7-Segment.circ as structural Verilog: 2 circuits, main circuit ripple adder
module FA (
  input  Cin,
  input  A,
  input  B,
  output out_4,
  output out_5
);

  wire and_1_out, and_2_out, xor_1_out;

  xor xor_1 (xor_1_out, A, B);
  and and_1 (and_1_out, Cin, xor_1_out);
  and and_2 (and_2_out, A, B);
  xor xor_2 (out_4, xor_1_out, Cin);
  or or_1 (out_5, and_1_out, and_2_out);
endmodule

module ripple_adder (
  input  in_1,
  input  [3:0] N_1,
  input  [3:0] N_2,
  output overflow
);

  wire and_1_out, and_2_out, and_3_out, and_4_out, and_5_out, and_6_out, and_7_out, and_8_out, and_9_out,
       and_10_out, and_11_out, and_12_out, and_13_out, and_14_out, and_15_out, and_16_out, and_17_out,
       and_18_out, and_19_out, and_20_out, and_21_out, and_22_out, and_23_out, and_24_out, and_25_out,
       and_26_out, and_27_out, fa_1_out_5, fa_2_out_5, LSB_out_5, or_1_out, or_2_out, or_3_out, or_4_out,
       or_5_out, or_6_out, or_7_out;
  wire [3:0] LSB_out_4;

  FA LSB (.Cin(in_1), .A(N_1[0]), .B(N_2[0]), .out_4(LSB_out_4[0]), .out_5(LSB_out_5));
  FA fa_1 (.Cin(LSB_out_5), .A(N_1[1]), .B(N_2[1]), .out_4(LSB_out_4[1]), .out_5(fa_1_out_5));
  FA fa_2 (.Cin(fa_1_out_5), .A(N_1[2]), .B(N_2[2]), .out_4(LSB_out_4[2]), .out_5(fa_2_out_5));
  FA MSB (.Cin(fa_2_out_5), .A(N_1[3]), .B(N_2[3]), .out_4(LSB_out_4[3]), .out_5(overflow));
  and and_1 (and_1_out, ~LSB_out_4[3], LSB_out_4[1]);  // AND_Gate
  and and_2 (and_2_out, ~LSB_out_4[3], LSB_out_4[2], LSB_out_4[0]);  // AND_Gate
  and and_3 (and_3_out, ~LSB_out_4[2], ~LSB_out_4[1], ~LSB_out_4[0]);  // AND_Gate
  and and_4 (and_4_out, LSB_out_4[3], ~LSB_out_4[2], ~LSB_out_4[1]);  // AND_Gate
  and and_5 (and_5_out, ~LSB_out_4[3], ~LSB_out_4[1], ~LSB_out_4[0]);  // AND_Gate
  and and_6 (and_6_out, ~LSB_out_4[2], ~LSB_out_4[1], ~LSB_out_4[0]);  // AND_Gate
  and and_7 (and_7_out, ~LSB_out_4[3], LSB_out_4[1], LSB_out_4[0]);  // AND_Gate
  and and_8 (and_8_out, ~LSB_out_4[3], ~LSB_out_4[2], LSB_out_4[1]);  // AND_Gate
  and and_9 (and_9_out, LSB_out_4[3], ~LSB_out_4[2], ~LSB_out_4[1]);  // AND_Gate
  and and_10 (and_10_out, ~LSB_out_4[3], LSB_out_4[2]);  // AND_Gate
  and and_11 (and_11_out, ~LSB_out_4[3], ~LSB_out_4[1], ~LSB_out_4[0]);  // AND_Gate
  and and_12 (and_12_out, ~LSB_out_4[3], LSB_out_4[1], LSB_out_4[0]);  // AND_Gate
  and and_13 (and_13_out, LSB_out_4[3], ~LSB_out_4[2], ~LSB_out_4[1]);  // AND_Gate
  and and_14 (and_14_out, ~LSB_out_4[3], LSB_out_4[2], ~LSB_out_4[1], LSB_out_4[0]);  // AND_Gate
  and and_15 (and_15_out, ~LSB_out_4[2], ~LSB_out_4[1], ~LSB_out_4[0]);  // AND_Gate
  and and_16 (and_16_out, ~LSB_out_4[3], ~LSB_out_4[2], LSB_out_4[1]);  // AND_Gate
  and and_17 (and_17_out, ~LSB_out_4[3], LSB_out_4[1], ~LSB_out_4[0]);  // AND_Gate
  and and_18 (and_18_out, ~LSB_out_4[2], ~LSB_out_4[1], ~LSB_out_4[0]);  // AND_Gate
  and and_19 (and_19_out, ~LSB_out_4[3], ~LSB_out_4[2], ~LSB_out_4[1]);  // AND_Gate
  and and_20 (and_20_out, ~LSB_out_4[3], LSB_out_4[1], ~LSB_out_4[0]);  // AND_Gate
  and and_21 (and_21_out, ~LSB_out_4[3], ~LSB_out_4[1]);  // AND_Gate
  and and_22 (and_22_out, LSB_out_4[3], ~LSB_out_4[2], ~LSB_out_4[1]);  // AND_Gate
  and and_23 (and_23_out, ~LSB_out_4[3], LSB_out_4[2], ~LSB_out_4[0], LSB_out_4[1]);  // AND_Gate
  and and_24 (and_24_out, LSB_out_4[3], ~LSB_out_4[2], ~LSB_out_4[1]);  // AND_Gate
  and and_25 (and_25_out, ~LSB_out_4[3], LSB_out_4[2], ~LSB_out_4[1]);  // AND_Gate
  and and_26 (and_26_out, ~LSB_out_4[3], ~LSB_out_4[2], LSB_out_4[1]);  // AND_Gate
  and and_27 (and_27_out, ~LSB_out_4[3], LSB_out_4[1], ~LSB_out_4[0]);  // AND_Gate
  or or_1 (or_1_out, and_1_out, and_2_out, and_3_out, and_4_out);
  or or_2 (or_2_out, and_5_out, and_6_out, and_7_out, and_8_out, and_9_out);
  or or_3 (or_3_out, and_10_out, and_11_out, and_12_out, and_13_out);
  or or_4 (or_4_out, and_14_out, and_15_out, and_16_out, and_17_out);
  or or_5 (or_5_out, and_18_out, and_19_out, and_20_out);
  or or_6 (or_6_out, and_21_out, and_22_out, and_23_out);
  or or_7 (or_7_out, and_24_out, and_25_out, and_26_out, and_27_out);
  _7_Segment_Display u_7_segment_display_1 (
    .g(or_7_out), .f(or_6_out), .a(or_1_out), .b(or_2_out), .e(or_5_out), .d(or_4_out), .c(or_3_out));  // open: dp
endmodule
