// Logisim project BCD-Gray.circ as structural Verilog: 1 circuit, main circuit main
module main (
  input  A1,
  input  A2,
  input  A3,
  input  A4,
  input  in_5,
  input  in_6,
  input  in_7,
  input  in_8,
  output G1,
  output G,
  output G3,
  output G4,
  output out_13,
  output out_14,
  output out_15,
  output out_16
);

  xor xor_1 (out_14, in_5, in_6);
  xor xor_2 (G, A1, A2);
  xor xor_3 (G3, A2, A3);
  xor xor_4 (G4, A3, A4);
  xor xor_5 (out_15, out_14, in_7);
  xor xor_6 (out_16, out_15, in_8);

  assign G1 = A1;
  assign out_13 = in_5;
endmodule
