// Logisim project 3b.circ as structural Verilog: 1 circuit, main circuit main
module main (
  input  in_1,
  output [2:0] out_2
);

  wire clock_1_out, j_k_ff_1_qn, j_k_ff_2_qn, multiplexer_1_out, multiplexer_2_out;

  Clock clock_1 (.out(clock_1_out));
  J_K_Flip_Flop j_k_ff_1 (
    .J(1'b1), .clk(clock_1_out), .K(1'b1), .Q(out_2[0]), .Qn(j_k_ff_1_qn));  // open: preset, en, reset
  Multiplexer multiplexer_1 (.in0(out_2[0]), .in1(j_k_ff_1_qn), .out(multiplexer_1_out), .sel(in_1));  // open: en
  J_K_Flip_Flop j_k_ff_2 (
    .J(1'b1), .clk(multiplexer_1_out), .K(1'b1), .Q(out_2[1]), .Qn(j_k_ff_2_qn));  // open: preset, en, reset
  Multiplexer multiplexer_2 (.in0(out_2[1]), .in1(j_k_ff_2_qn), .out(multiplexer_2_out), .sel(in_1));  // open: en
  J_K_Flip_Flop j_k_ff_3 (.J(1'b1), .clk(multiplexer_2_out), .K(1'b1), .Q(out_2[2]));  // open: Qn, preset, en, reset
  LED led_1 (.in(out_2[0]));
  LED led_2 (.in(out_2[1]));
  LED led_3 (.in(out_2[2]));
endmodule
