// Logisim project 3rd.circ as structural Verilog: 1 circuit, main circuit main
module main (
  output [2:0] out_1
);

  wire clock_1_out, j_k_ff_1_qn, j_k_ff_2_qn;

  Clock clock_1 (.out(clock_1_out));
  J_K_Flip_Flop j_k_ff_1 (
    .J(1'b1), .clk(clock_1_out), .K(1'b1), .Q(out_1[0]), .Qn(j_k_ff_1_qn));  // open: preset, en, reset
  J_K_Flip_Flop j_k_ff_2 (
    .J(1'b1), .clk(j_k_ff_1_qn), .K(1'b1), .Q(out_1[1]), .Qn(j_k_ff_2_qn));  // open: preset, en, reset
  J_K_Flip_Flop j_k_ff_3 (.J(1'b1), .clk(j_k_ff_2_qn), .K(1'b1), .Q(out_1[2]));  // open: Qn, preset, en, reset
  LED led_1 (.in(out_1[0]));
  LED led_2 (.in(out_1[1]));
  LED led_3 (.in(out_1[2]));
endmodule
