// Logisim project Q1.circ as structural Verilog: 4 circuits, main circuit main
module main (
  input  [4:0] in_1,
  input  [4:0] in_2
);

  wire leftbcd_1_a_2, leftbcd_1_b_2, leftbcd_1_c_2, leftbcd_1_d_2, leftbcd_1_e_2, leftbcd_1_f, leftbcd_1_g,
       nextbcd_1_a_2, nextbcd_1_b_2, nextbcd_1_c_2, nextbcd_1_d_2, nextbcd_1_e_2, nextbcd_1_f, nextbcd_1_g;
  wire [4:0] adder_1_out;

  Adder #(.width(5)) adder_1 (.a(in_1), .b(in_2), .out(adder_1_out), .cin(1'b0));  // open: cout
  LeftBCD leftbcd_1 (
    .E(adder_1_out[4]), .D(adder_1_out[3]), .C(adder_1_out[2]), .B(adder_1_out[1]), .A(adder_1_out[0]),
    .a_2(leftbcd_1_a_2), .b_2(leftbcd_1_b_2), .c_2(leftbcd_1_c_2), .d_2(leftbcd_1_d_2), .e_2(leftbcd_1_e_2),
    .f(leftbcd_1_f), .g(leftbcd_1_g));
  nextBCD nextbcd_1 (
    .E(adder_1_out[4]), .D(adder_1_out[3]), .C(adder_1_out[2]), .B(adder_1_out[1]), .A(adder_1_out[0]),
    .a_2(nextbcd_1_a_2), .b_2(nextbcd_1_b_2), .c_2(nextbcd_1_c_2), .d_2(nextbcd_1_d_2), .e_2(nextbcd_1_e_2),
    .f(nextbcd_1_f), .g(nextbcd_1_g));
  _7_Segment_Display u_7_segment_display_1 (
    .g(leftbcd_1_g), .f(leftbcd_1_f), .a(leftbcd_1_a_2), .b(leftbcd_1_b_2), .e(leftbcd_1_e_2),
    .d(leftbcd_1_d_2), .c(leftbcd_1_c_2));  // open: dp
  _7_Segment_Display u_7_segment_display_2 (
    .g(nextbcd_1_g), .f(nextbcd_1_f), .a(nextbcd_1_a_2), .b(nextbcd_1_b_2), .e(nextbcd_1_e_2),
    .d(nextbcd_1_d_2), .c(nextbcd_1_c_2));  // open: dp
endmodule

module bcd (
  input  D,
  input  C,
  input  B,
  input  A,
  output a_2,
  output b_2,
  output c_2,
  output d_2,
  output e,
  output f,
  output g
);

  wire and_1_out, and_2_out, and_3_out, and_4_out, and_5_out, and_6_out, and_7_out, and_8_out, and_9_out,
       and_10_out, and_11_out, and_12_out, and_13_out, and_14_out, and_15_out, and_16_out, not_1_out,
       not_2_out, not_3_out, not_4_out, not_5_out, not_6_out, not_7_out, not_8_out, not_9_out, not_10_out,
       not_11_out, not_12_out, not_13_out, not_14_out, not_15_out, not_16_out, not_17_out, not_18_out,
       not_19_out, not_20_out, not_21_out;

  not not_1 (not_1_out, C);
  and and_1 (and_1_out, not_1_out, not_2_out);
  not not_2 (not_2_out, A);
  and and_2 (and_2_out, C, A);
  not not_3 (not_3_out, C);
  not not_4 (not_4_out, B);
  and and_3 (and_3_out, not_4_out, not_5_out);
  not not_5 (not_5_out, A);
  and and_4 (and_4_out, B, A);
  not not_6 (not_6_out, B);
  or or_1 (c_2, not_6_out, A, C);
  not not_7 (not_7_out, C);
  and and_5 (and_5_out, not_7_out, not_8_out);
  not not_8 (not_8_out, A);
  not not_9 (not_9_out, C);
  and and_6 (and_6_out, not_9_out, B);
  and and_7 (and_7_out, B, not_10_out);
  not not_10 (not_10_out, A);
  not not_11 (not_11_out, B);
  and and_8 (and_8_out, C, not_11_out, A);
  not not_12 (not_12_out, C);
  and and_9 (and_9_out, not_12_out, not_13_out);
  not not_13 (not_13_out, A);
  and and_10 (and_10_out, B, not_14_out);
  not not_14 (not_14_out, A);
  not not_15 (not_15_out, B);
  and and_11 (and_11_out, not_15_out, not_16_out);
  not not_16 (not_16_out, A);
  and and_12 (and_12_out, C, not_17_out);
  not not_17 (not_17_out, B);
  and and_13 (and_13_out, C, not_18_out);
  not not_18 (not_18_out, A);
  not not_19 (not_19_out, C);
  and and_14 (and_14_out, not_19_out, B);
  and and_15 (and_15_out, C, not_20_out);
  not not_20 (not_20_out, B);
  and and_16 (and_16_out, C, not_21_out);
  not not_21 (not_21_out, A);
  or or_2 (a_2, and_1_out, B, and_2_out, D);
  or or_3 (b_2, not_3_out, and_3_out, and_4_out);
  or or_4 (d_2, and_5_out, and_6_out, and_7_out, and_8_out, D);
  or or_5 (e, and_9_out, and_10_out);
  or or_6 (f, and_11_out, and_12_out, and_13_out, D);
  or or_7 (g, and_14_out, and_15_out, and_16_out, D);
endmodule

module nextBCD (
  input  E,
  input  D,
  input  C,
  input  B,
  input  A,
  output a_2,
  output b_2,
  output c_2,
  output d_2,
  output e_2,
  output f,
  output g
);

  wire and_1_out, and_2_out, and_3_out, and_4_out, and_5_out, and_6_out, and_7_out, and_8_out, and_9_out,
       and_10_out, and_11_out, and_12_out, and_13_out, and_14_out, and_15_out, and_16_out, and_17_out,
       and_18_out, and_19_out, and_20_out, and_21_out, and_22_out, and_23_out, and_24_out, and_25_out,
       and_26_out, and_27_out, and_28_out, and_29_out, and_30_out, and_31_out, and_32_out, and_33_out,
       and_34_out, and_35_out, and_36_out, and_37_out, and_38_out, and_39_out, and_40_out, not_1_out,
       not_2_out, not_3_out, not_4_out, not_5_out, not_6_out, not_7_out, not_8_out, not_9_out, not_10_out,
       not_11_out, not_12_out, not_13_out, not_14_out, not_15_out, not_16_out, not_17_out, not_18_out,
       not_19_out, not_20_out, not_21_out, not_22_out, not_23_out, not_24_out, not_25_out, not_26_out,
       not_27_out, not_28_out, not_29_out, not_30_out, not_31_out, not_32_out, not_33_out, not_34_out,
       not_35_out, not_36_out, not_37_out, not_38_out, not_39_out, not_40_out, not_41_out, not_42_out,
       not_43_out, not_44_out, not_45_out, not_46_out, not_47_out, not_48_out;

  not not_1 (not_1_out, C);
  not not_2 (not_2_out, A);
  not not_3 (not_3_out, D);
  not not_4 (not_4_out, B);
  not not_5 (not_5_out, E);
  not not_6 (not_6_out, C);
  not not_7 (not_7_out, E);
  not not_8 (not_8_out, B);
  not not_9 (not_9_out, A);
  not not_10 (not_10_out, C);
  not not_11 (not_11_out, D);
  not not_12 (not_12_out, B);
  not not_13 (not_13_out, A);
  not not_14 (not_14_out, D);
  not not_15 (not_15_out, B);
  not not_16 (not_16_out, C);
  not not_17 (not_17_out, C);
  not not_18 (not_18_out, A);
  not not_19 (not_19_out, D);
  not not_20 (not_20_out, C);
  not not_21 (not_21_out, D);
  not not_22 (not_22_out, A);
  not not_23 (not_23_out, B);
  not not_24 (not_24_out, B);
  not not_25 (not_25_out, C);
  not not_26 (not_26_out, A);
  not not_27 (not_27_out, D);
  not not_28 (not_28_out, A);
  not not_29 (not_29_out, B);
  not not_30 (not_30_out, A);
  not not_31 (not_31_out, D);
  not not_32 (not_32_out, B);
  not not_33 (not_33_out, A);
  not not_34 (not_34_out, D);
  not not_35 (not_35_out, B);
  not not_36 (not_36_out, D);
  not not_37 (not_37_out, A);
  not not_38 (not_38_out, C);
  not not_39 (not_39_out, B);
  not not_40 (not_40_out, C);
  not not_41 (not_41_out, A);
  not not_42 (not_42_out, A);
  not not_43 (not_43_out, D);
  not not_44 (not_44_out, C);
  not not_45 (not_45_out, B);
  not not_46 (not_46_out, A);
  not not_47 (not_47_out, B);
  not not_48 (not_48_out, A);
  and and_1 (and_1_out, not_1_out, not_2_out);
  and and_2 (and_2_out, not_3_out, B);
  and and_3 (and_3_out, C, A);
  and and_4 (and_4_out, D, not_4_out);
  and and_5 (and_5_out, not_5_out, not_6_out);
  and and_6 (and_6_out, not_7_out, not_8_out, not_9_out);
  and and_7 (and_7_out, not_10_out, A);
  and and_8 (and_8_out, not_11_out, B, A);
  and and_9 (and_9_out, D, not_12_out);
  and and_10 (and_10_out, D, not_13_out);
  and and_11 (and_11_out, E, B);
  and and_12 (and_12_out, not_14_out, not_15_out);
  and and_13 (and_13_out, C, B);
  and and_14 (and_14_out, D, not_16_out);
  and and_15 (and_15_out, not_17_out, not_18_out);
  and and_16 (and_16_out, not_19_out, not_20_out, B);
  and and_17 (and_17_out, not_21_out, B, not_22_out);
  and and_18 (and_18_out, C, not_23_out, A);
  and and_19 (and_19_out, D, not_24_out);
  and and_20 (and_20_out, D, C, A);
  and and_21 (and_21_out, E, C);
  and and_22 (and_22_out, not_25_out, not_26_out);
  and and_23 (and_23_out, not_27_out, B, not_28_out);
  and and_24 (and_24_out, D, not_29_out, not_30_out);
  and and_25 (and_25_out, E, C);
  and and_26 (and_26_out, not_31_out, not_32_out, not_33_out);
  and and_27 (and_27_out, not_34_out, C, not_35_out);
  and and_28 (and_28_out, not_36_out, C, not_37_out);
  and and_29 (and_29_out, D, not_38_out, not_39_out);
  and and_30 (and_30_out, D, not_40_out, not_41_out);
  and and_31 (and_31_out, D, C, B);
  and and_32 (and_32_out, E, not_42_out);
  and and_33 (and_33_out, E, C);
  and and_34 (and_34_out, not_43_out, not_44_out, B);
  and and_35 (and_35_out, C, not_45_out);
  and and_36 (and_36_out, C, not_46_out);
  and and_37 (and_37_out, D, not_47_out);
  and and_38 (and_38_out, D, C);
  and and_39 (and_39_out, E, not_48_out);
  and and_40 (and_40_out, E, C);
  or or_1 (a_2, and_1_out, and_2_out, and_3_out, and_4_out, E);
  or or_2 (b_2, and_5_out, and_6_out, and_7_out, and_8_out, and_9_out, and_10_out, and_11_out);
  or or_3 (c_2, and_12_out, A, and_13_out, and_14_out, E);
  or or_4 (d_2, and_15_out, and_16_out, and_17_out, and_18_out, and_19_out, and_20_out, and_21_out);
  or or_5 (e_2, and_22_out, and_23_out, and_24_out, and_25_out);
  or or_6 (f, and_26_out, and_27_out, and_28_out, and_29_out, and_30_out, and_31_out, and_32_out, and_33_out);
  or or_7 (g, and_34_out, and_35_out, and_36_out, and_37_out, and_38_out, and_39_out, and_40_out);
endmodule

module LeftBCD (
  input  E,
  input  D,
  input  C,
  input  B,
  input  A,
  output a_2,
  output b_2,
  output c_2,
  output d_2,
  output e_2,
  output f,
  output g
);

  wire and_1_out, and_2_out, and_3_out, and_4_out, and_5_out, and_6_out, and_7_out, and_8_out, not_1_out,
       not_2_out, not_3_out, not_4_out, not_5_out, not_6_out, not_7_out, not_8_out, not_9_out, not_10_out,
       not_11_out, not_12_out, not_13_out, not_14_out, not_15_out, not_16_out, not_17_out, not_18_out,
       not_19_out, not_20_out;

  not not_1 (not_1_out, E);
  not not_2 (not_2_out, D);
  not not_3 (not_3_out, E);
  not not_4 (not_4_out, C);
  not not_5 (not_5_out, B);
  not not_6 (not_6_out, E);
  not not_7 (not_7_out, D);
  not not_8 (not_8_out, E);
  not not_9 (not_9_out, C);
  not not_10 (not_10_out, B);
  not not_11 (not_11_out, E);
  not not_12 (not_12_out, D);
  not not_13 (not_13_out, E);
  not not_14 (not_14_out, C);
  not not_15 (not_15_out, B);
  not not_16 (not_16_out, E);
  not not_17 (not_17_out, D);
  not not_18 (not_18_out, E);
  not not_19 (not_19_out, C);
  not not_20 (not_20_out, B);
  and and_1 (and_1_out, not_1_out, not_2_out);
  and and_2 (and_2_out, not_3_out, not_4_out, not_5_out);
  and and_3 (and_3_out, not_6_out, not_7_out);
  and and_4 (and_4_out, not_8_out, not_9_out, not_10_out);
  and and_5 (and_5_out, not_11_out, not_12_out);
  and and_6 (and_6_out, not_13_out, not_14_out, not_15_out);
  and and_7 (and_7_out, not_16_out, not_17_out);
  and and_8 (and_8_out, not_18_out, not_19_out, not_20_out);
  or or_1 (a_2, and_1_out, and_2_out);
  or or_2 (d_2, and_3_out, and_4_out);
  or or_3 (e_2, and_5_out, and_6_out);
  or or_4 (f, and_7_out, and_8_out);

  assign b_2 = 1'b1;
  assign c_2 = 1'b1;
  assign g = 1'b0;
endmodule
