// Logisim project Q1.circ as structural Verilog: 1 circuit, main circuit main
module main (
  output [2:0] out_1
);

  wire and_1_out, clock_1_out, nor_1_out, xor_1_out;

  Clock clock_1 (.out(clock_1_out));
  nor nor_1 (nor_1_out, out_1[0], out_1[2]);
  D_Flip_Flop d_ff_1 (.clk(clock_1_out), .D(nor_1_out), .Q(out_1[0]));  // open: Qn, preset, en, reset
  xor xor_1 (xor_1_out, out_1[1], out_1[0]);
  D_Flip_Flop d_ff_2 (.clk(clock_1_out), .D(xor_1_out), .Q(out_1[1]));  // open: Qn, preset, en, reset
  and and_1 (and_1_out, out_1[1], out_1[0]);
  D_Flip_Flop d_ff_3 (.clk(clock_1_out), .D(and_1_out), .Q(out_1[2]));  // open: Qn, preset, en, reset
endmodule
