// Logisim project Q3.circ as structural Verilog: 4 circuits, main circuit q1_201ec164
module q1_201ec164 (
  output [2:0] out_1
);

  wire and_1_out, and_2_out, and_3_out, clock_1_out, undriven, undriven_2, xor_1_out;

  Clock clock_1 (.out(clock_1_out));
  and and_1 (and_1_out, out_1[0], out_1[1], undriven);
  // D_Flip_Flop d_ff_1: pin names not known; wires that end beside it: and_1_out, clock_1_out
  ExactlyOne xor_1 (.out(xor_1_out), .in1(out_1[0]), .in3(out_1[1]), .in4(undriven));
  and and_2 (and_2_out, undriven, xor_1_out);
  // D_Flip_Flop d_ff_2: pin names not known; wires that end beside it: and_2_out, clock_1_out
  and and_3 (and_3_out, undriven, undriven_2);
  // D_Flip_Flop d_ff_3: pin names not known; wires that end beside it: and_3_out, clock_1_out
endmodule

module q2_201ec164 (
  input  S,
  output [3:0] out_2
);

  wire and_1_out, and_2_out, and_3_out, and_4_out, and_5_out, and_6_out, clock_1_out, not_1_out, or_1_out,
       or_2_out, or_3_out, undriven, undriven_2, undriven_3;

  Clock clock_1 (.out(clock_1_out));
  not not_1 (not_1_out, S);
  J_K_Flip_Flop j_k_ff_1 (.clk(1'b1), .en(1'b1), .reset(1'b1));  // open: J, K, Q, Qn, preset
  and and_1 (and_1_out, not_1_out, out_2[0]);
  and and_2 (and_2_out, S, undriven);
  J_K_Flip_Flop j_k_ff_2 (.en(or_1_out), .reset(or_1_out));  // open: J, clk, K, Q, Qn, preset
  or or_1 (or_1_out, and_1_out, and_2_out);
  and and_3 (and_3_out, and_1_out, out_2[1]);
  or or_2 (or_2_out, and_3_out, and_4_out);
  and and_4 (and_4_out, undriven_2, and_2_out);
  J_K_Flip_Flop j_k_ff_3 (.en(or_2_out), .reset(or_2_out));  // open: J, clk, K, Q, Qn, preset
  and and_5 (and_5_out, and_3_out, out_2[2]);
  and and_6 (and_6_out, undriven_3, and_4_out, clock_1_out);
  J_K_Flip_Flop j_k_ff_4 (.K(or_3_out), .en(or_3_out), .reset(or_3_out));  // open: J, clk, Q, Qn, preset
  or or_3 (or_3_out, and_5_out, and_6_out);

  // Notes on the sheet:
  //   s:0 up counter / s:1 down counter
endmodule

module q3_201ec164 (
  output [3:0] out_1
);

  wire and_1_out, and_2_out, and_3_out, and_4_out, and_5_out, and_6_out, and_7_out, and_8_out, and_9_out,
       and_10_out, and_11_out, and_12_out, and_13_out, clock_1_out, d_ff_1_qn, d_ff_2_qn, d_ff_3_qn,
       d_ff_4_qn, or_1_out, or_2_out, or_3_out, or_4_out;

  or or_1 (or_1_out, and_1_out, and_2_out, and_3_out);
  Clock clock_1 (.out(clock_1_out));
  and and_1 (and_1_out, out_1[0], d_ff_3_qn, out_1[2], out_1[3]);
  and and_2 (and_2_out, d_ff_4_qn, out_1[1], out_1[2], d_ff_1_qn);
  and and_3 (and_3_out, d_ff_4_qn, d_ff_3_qn);
  D_Flip_Flop d_ff_1 (.clk(clock_1_out), .D(or_1_out), .Q(out_1[3]), .Qn(d_ff_1_qn));  // open: preset, en, reset
  and and_4 (and_4_out, out_1[3], d_ff_4_qn, d_ff_3_qn);
  or or_2 (or_2_out, and_4_out, and_5_out, and_6_out);
  and and_5 (and_5_out, out_1[3], d_ff_2_qn, out_1[1], out_1[0]);
  D_Flip_Flop d_ff_2 (.clk(clock_1_out), .D(or_2_out), .Q(out_1[2]), .Qn(d_ff_2_qn));  // open: preset, en, reset
  and and_6 (and_6_out, d_ff_1_qn, out_1[2], out_1[1], d_ff_4_qn);
  and and_7 (and_7_out, out_1[3], out_1[2], d_ff_3_qn);
  or or_3 (or_3_out, and_7_out, and_8_out, and_9_out);
  and and_8 (and_8_out, d_ff_1_qn, out_1[2], out_1[0], out_1[1]);
  D_Flip_Flop d_ff_3 (.clk(clock_1_out), .D(or_3_out), .Q(out_1[1]), .Qn(d_ff_3_qn));  // open: preset, en, reset
  and and_9 (and_9_out, out_1[3], d_ff_2_qn, out_1[1], out_1[0]);
  and and_10 (and_10_out, d_ff_1_qn, d_ff_2_qn, out_1[0]);
  or or_4 (or_4_out, and_10_out, and_11_out, and_12_out, and_13_out);
  and and_11 (and_11_out, d_ff_2_qn, out_1[1], out_1[0]);
  and and_12 (and_12_out, d_ff_1_qn, out_1[2], out_1[1]);
  and and_13 (and_13_out, out_1[2], out_1[3], d_ff_3_qn, out_1[0]);
  D_Flip_Flop d_ff_4 (.clk(clock_1_out), .D(or_4_out), .Q(out_1[0]), .Qn(d_ff_4_qn));  // open: preset, en, reset
endmodule

module q4 (
  output [5:0] out_1
);

  wire clock_1_out, counter_1_p1, not_1_out, not_2_out;

  Clock clock_1 (.out(clock_1_out));
  // Counter #(.width(6), .max('h3f)) counter_1: pin names not known; wires that end beside it: counter_1_p1, counter_1_p1, 1'b0, 1'b1
  and and_1 (counter_1_p1, not_1_out, not_2_out, out_1[2], out_1[3], out_1[4], out_1[5]);
  not not_1 (not_1_out, out_1[0]);
  not not_2 (not_2_out, out_1[1]);
endmodule
