// Logisim project Endsem.circ as structural Verilog: 1 circuit, main circuit main
module main (
  output out_1,
  output out_2,
  output out_3
);

  wire and_1_out, clock_1_out, not_1_out, not_2_out, not_3_out, or_1_out;

  Clock clock_1 (.out(clock_1_out));
  or or_1 (or_1_out, out_1, not_1_out);
  not not_1 (not_1_out, out_2);
  J_K_Flip_Flop Q1 (.J(or_1_out), .clk(clock_1_out), .K(1'b1), .Q(out_3));  // open: Qn, preset, en, reset
  not not_2 (not_2_out, out_3);
  not not_3 (not_3_out, out_3);
  J_K_Flip_Flop Q2 (.J(not_3_out), .clk(clock_1_out), .K(not_3_out), .Q(out_2));  // open: Qn, preset, en, reset
  and and_1 (and_1_out, not_2_out, out_2);
  J_K_Flip_Flop Q3 (.J(and_1_out), .clk(clock_1_out), .K(and_1_out), .Q(out_1));  // open: Qn, preset, en, reset
endmodule
