// Logisim project EndsemFinAL.circ as structural Verilog: 2 circuits, main circuit main
module main (
);

  wire and_1_out, bcd_1__2_2, bcd_1__3_2, bcd_1__4, bcd_1__5, bcd_1__6, bcd_1__7, bcd_1__8, clock_1_out,
       not_1_out, not_2_out, not_3_out, or_1_out, Q1_q, Q2_q, Q3_q;

  Clock clock_1 (.out(clock_1_out));
  or or_1 (or_1_out, Q3_q, not_1_out);
  not not_1 (not_1_out, Q2_q);
  J_K_Flip_Flop Q1 (.J(or_1_out), .clk(clock_1_out), .K(1'b1), .Q(Q1_q));  // open: Qn, preset, en, reset
  not not_2 (not_2_out, Q1_q);
  not not_3 (not_3_out, Q1_q);
  J_K_Flip_Flop Q2 (.J(not_3_out), .clk(clock_1_out), .K(not_3_out), .Q(Q2_q));  // open: Qn, preset, en, reset
  and and_1 (and_1_out, not_2_out, Q2_q);
  J_K_Flip_Flop Q3 (.J(and_1_out), .clk(clock_1_out), .K(and_1_out), .Q(Q3_q));  // open: Qn, preset, en, reset
  bcd bcd_1 (
    ._3(1'b0), ._2(Q3_q), ._1(Q2_q), ._0(Q1_q), ._5(bcd_1__5), ._8(bcd_1__8), ._7(bcd_1__7), ._6(bcd_1__6),
    ._4(bcd_1__4), ._3_2(bcd_1__3_2), ._2_2(bcd_1__2_2));
  _7_Segment_Display u_7_segment_display_1 (
    .g(bcd_1__5), .f(bcd_1__6), .a(bcd_1__7), .b(bcd_1__8), .e(bcd_1__2_2), .d(bcd_1__3_2), .c(bcd_1__4));  // open: dp
endmodule

module bcd (
  input  _3,
  input  _2,
  input  _1,
  input  _0,
  output _5,
  output _8,
  output _7,
  output _6,
  output _4,
  output _3_2,
  output _2_2
);

  wire and_1_out, and_2_out, and_3_out, and_4_out, and_5_out, and_6_out, and_7_out, and_8_out, and_9_out,
       and_10_out, and_11_out, and_12_out, and_13_out, and_14_out, and_15_out, and_16_out, and_17_out,
       and_18_out, and_19_out, and_20_out, and_21_out, and_22_out, and_23_out, and_24_out, and_25_out,
       and_26_out, and_27_out;

  and and_1 (and_1_out, ~_3, _1);  // AND_Gate
  and and_2 (and_2_out, ~_3, _2, _0);  // AND_Gate
  and and_3 (and_3_out, ~_2, ~_1, ~_0);  // AND_Gate
  and and_4 (and_4_out, _3, ~_2, ~_1);  // AND_Gate
  and and_5 (and_5_out, ~_3, ~_1, ~_0);  // AND_Gate
  and and_6 (and_6_out, ~_2, ~_1, ~_0);  // AND_Gate
  and and_7 (and_7_out, ~_3, _1, _0);  // AND_Gate
  and and_8 (and_8_out, ~_3, ~_2, _1);  // AND_Gate
  and and_9 (and_9_out, _3, ~_2, ~_1);  // AND_Gate
  and and_10 (and_10_out, ~_3, _2);  // AND_Gate
  and and_11 (and_11_out, ~_3, ~_1, ~_0);  // AND_Gate
  and and_12 (and_12_out, ~_3, _1, _0);  // AND_Gate
  and and_13 (and_13_out, _3, ~_2, ~_1);  // AND_Gate
  and and_14 (and_14_out, ~_3, _2, ~_1, _0);  // AND_Gate
  and and_15 (and_15_out, ~_2, ~_1, ~_0);  // AND_Gate
  and and_16 (and_16_out, ~_3, ~_2, _1);  // AND_Gate
  and and_17 (and_17_out, ~_3, _1, ~_0);  // AND_Gate
  and and_18 (and_18_out, ~_2, ~_1, ~_0);  // AND_Gate
  and and_19 (and_19_out, ~_3, ~_2, ~_1);  // AND_Gate
  and and_20 (and_20_out, ~_3, _1, ~_0);  // AND_Gate
  and and_21 (and_21_out, ~_3, ~_1);  // AND_Gate
  and and_22 (and_22_out, _3, ~_2, ~_1);  // AND_Gate
  and and_23 (and_23_out, ~_3, _2, ~_0, _1);  // AND_Gate
  and and_24 (and_24_out, _3, ~_2, ~_1);  // AND_Gate
  and and_25 (and_25_out, ~_3, _2, ~_1);  // AND_Gate
  and and_26 (and_26_out, ~_3, ~_2, _1);  // AND_Gate
  and and_27 (and_27_out, ~_3, _1, ~_0);  // AND_Gate
  or or_1 (_7, and_1_out, and_2_out, and_3_out, and_4_out);
  or or_2 (_8, and_5_out, and_6_out, and_7_out, and_8_out, and_9_out);
  or or_3 (_4, and_10_out, and_11_out, and_12_out, and_13_out);
  or or_4 (_3_2, and_14_out, and_15_out, and_16_out, and_17_out);
  or or_5 (_2_2, and_18_out, and_19_out, and_20_out);
  or or_6 (_6, and_21_out, and_22_out, and_23_out);
  or or_7 (_5, and_24_out, and_25_out, and_26_out, and_27_out);
endmodule
