// Logisim project 3B.circ as structural Verilog: 1 circuit, main circuit main
module main (
  input  C,
  input  D,
  input  in_3,
  input  [1:0] in_4,
  output out_5
);

  wire and_1_out, or_1_out, undriven;

  or or_1 (or_1_out, D, C);
  and and_1 (and_1_out, C, D);
  Multiplexer #(.select(2)) multiplexer_1 (
    .in0(and_1_out), .in1(and_1_out), .in2(and_1_out), .in3(or_1_out), .out(out_5), .sel(in_4), .en(undriven));
endmodule
