// Logisim project Q3.circ as structural Verilog: 1 circuit, main circuit main
// B+D
module main (
  input  A,
  input  B,
  input  C,
  input  D,
  output out_5
);

  wire A_B_out, A_C_out, A_D_out, B_C_out, B_D_out, C_D_out;

  nor A_B (A_B_out, A, B);
  nor A_C (A_C_out, A, C);
  nor B_C (B_C_out, C, B);
  nor A_D (A_D_out, A, D);
  nor C_D (C_D_out, D, C);
  nor B_D (B_D_out, D, B);
  nor nor_1 (out_5, B_D_out, A_C_out, B_C_out, A_D_out, A_B_out, C_D_out);
endmodule
