// Logisim project Q5.circ as structural Verilog: 1 circuit, main circuit main
module main (
  input  in_1,
  input  A0,
  input  b0,
  input  A1,
  input  b1,
  input  A2,
  input  b2,
  input  b3,
  input  A3,
  output out_10,
  output out_11,
  output out_12,
  output out_13,
  output out_14
);

  wire adder_1_cout, adder_2_cout, adder_3_cout, xor_1_out, xor_2_out, xor_3_out, xor_4_out;

  xor xor_1 (xor_1_out, in_1, b0);
  xor xor_2 (xor_2_out, in_1, b1);
  xor xor_3 (xor_3_out, in_1, b2);
  xor xor_4 (xor_4_out, in_1, b3);
  Adder #(.width(1)) adder_1 (.a(A0), .b(xor_1_out), .out(out_10), .cin(in_1), .cout(adder_1_cout));
  Adder #(.width(1)) adder_2 (.a(A1), .b(xor_2_out), .out(out_11), .cin(adder_1_cout), .cout(adder_2_cout));
  Adder #(.width(1)) adder_3 (.a(A2), .b(xor_3_out), .out(out_12), .cin(adder_2_cout), .cout(adder_3_cout));
  Adder #(.width(1)) adder_4 (.a(A3), .b(xor_4_out), .out(out_13), .cin(adder_3_cout), .cout(out_14));
endmodule
